# Fritzing sketch PlatineSlave (saved by Fritzing 0.9.10b)
circuit board: 9.04702cm x 6.48034cm
breadboards: 1
perfboards: 1

parts:
  +5V = female pin header, 2 pins [form="♀ (female)"]
  M1 = Stepper Motor - Bipolar
  M2 = Stepper Motor - Bipolar
  M3 = Stepper Motor - Bipolar
  M4 = Stepper Motor - Bipolar
  M5 = Stepper Motor - Bipolar
  M6 = Stepper Motor - Bipolar
  J2 = Basic Servo
  J3 = Basic Servo
  Upper_Lid = Basic Servo
  Lower_Lid = Basic Servo
  Eye_L/R = Basic Servo
  Eye_U/D = Basic Servo
  Pupil = Basic Servo
  J9 = female pin header, 2 pins [form="♀ (female)"]
  J10 = female pin header, 2 pins [form="♀ (female)"]
  J11 = female pin header, 2 pins [form="♀ (female)"]
  J12 = female pin header, 2 pins [form="♀ (female)"]
  J13 = female pin header, 2 pins [form="♀ (female)"]
  J14 = female pin header, 2 pins [form="♀ (female)"]
  J15 = female pin header, 2 pins [form="♀ (female)"]
  J16 = female pin header, 2 pins [form="♀ (female)"]
  J17 = female pin header, 2 pins [form="♀ (female)"]
  J18 = female pin header, 2 pins [form="♀ (female)"]
  J19 = female pin header, 2 pins [form="♀ (female)"]
  J20 = female pin header, 2 pins [form="♀ (female)"]
  J21 = female pin header, 2 pins [form="♀ (female)"]
  J22 = female pin header, 2 pins [form="♀ (female)"]
  J23 = female pin header, 2 pins [form="♀ (female)"]
  J24 = female pin header, 2 pins [form="♀ (female)"]
  J25 = female pin header, 2 pins [form="♀ (female)"]
  J26 = female pin header, 2 pins [form="♀ (female)"]
  J27 = female pin header, 2 pins [form="♀ (female)"]
  J28 = female pin header, 2 pins [form="♀ (female)"]
  J29 = female pin header, 2 pins [form="♀ (female)"]
  J30 = female pin header, 2 pins [form="♀ (female)"]
  J31 = female pin header, 2 pins [form="♀ (female)"]
  J32 = female pin header, 2 pins [form="♀ (female)"]
  M7 = Stepper Motor - Bipolar
  M8 = Stepper Motor - Bipolar
  M9 = Stepper Motor - Bipolar
  J33 = Basic Servo
  M10 = Stepper Motor - Bipolar
  M11 = Stepper Motor - Bipolar
  M12 = Stepper Motor - Bipolar
  J34 = Basic Servo

nets:
  GND: +5V.pin1, M1.B, Upper_Lid.gnd, Lower_Lid.gnd, Eye_L/R.gnd, Eye_U/D.gnd, Pupil.pulse, J9.pin1, J9.pin2, J10.pin1, J10.pin2, J11.pin1, J11.pin2, J12.pin1, J12.pin2, J13.pin1, J13.pin2, J14.pin1, J14.pin2, J15.pin1, J15.pin2, J16.pin1, J16.pin2, J17.pin1, J17.pin2, J18.pin1, J18.pin2, J19.pin1, J19.pin2, J20.pin1, J20.pin2, M7.B
  N1: +5V.pin2, M1.D, Upper_Lid.pulse, Lower_Lid.pulse, Eye_L/R.pulse, Eye_U/D.pulse, Pupil.gnd, J21.pin1, J21.pin2, J22.pin1, J22.pin2, J23.pin1, J23.pin2, J24.pin1, J24.pin2, J25.pin1, J25.pin2, J26.pin1, J26.pin2, J27.pin1, J27.pin2, J28.pin1, J28.pin2, J29.pin1, J29.pin2, J30.pin1, J30.pin2, J31.pin1, J31.pin2, J32.pin1, J32.pin2, M7.D
  N2: M1.A, Lower_Lid.vcc, M7.A
  N3: M1.C, Eye_L/R.vcc, M7.C
  N4: M2.A, M10.A
  N5: M2.C, Eye_U/D.vcc, M10.C
  N6: M2.B, M10.B
  N7: M2.D, M10.D
  N8: M3.A, M11.A
  N9: M3.C, M11.C
  N10: M3.B, M11.B
  N11: M3.D, M11.D
  N12: M4.A, M12.A
  N13: M4.C, M12.C
  N14: M4.B, M12.B
  N15: M4.D, M12.D
  N16: M5.A, M8.A
  N17: M5.C, M8.C
  N18: M5.B, M8.B
  N19: M5.D, Upper_Lid.vcc, M8.D
  N20: M6.A, M9.A
  N21: M6.C, M9.C
  N22: M6.B, M9.B
  N23: M6.D, M9.D
  GND_2: J2.gnd, J34.gnd
  VCC: J2.vcc, J34.vcc
  N24: J2.pulse, J34.pulse
  GND_3: J3.gnd, J33.gnd
  VCC_2: J3.vcc, J33.vcc
  N25: J3.pulse, J33.pulse

notes:
  GND
  +5V
  WWW.CALMYJANE.COM
